// Logisim project Programa_Principal.circ as structural Verilog: 8 circuits, main circuit ALU_1bit
module main (
  input  Operacion,
  input  [1:0] Accion,
  input  [1:0] Registro,
  input  [1:0] Banco,
  input  [7:0] Numero,
  input  [7:0] in_6,
  input  [7:0] in_7,
  input  [1:0] in_8,
  input  [15:0] ENTRADA,
  input  Clear_Cache,
  output [7:0] out_11,
  output [7:0] out_12,
  output [7:0] out_13,
  output [7:0] out_14,
  output [7:0] out_15,
  output [7:0] out_16,
  output out_17,
  output [7:0] out_18
);

  wire CLK;
  wire [1:0] modulo_decoder_banco_1_code, modulo_decoder_banco_1_num_reg, modulo_decoder_banco_2_code,
       modulo_decoder_banco_2_num_reg, modulo_decoder_banco_3_code, modulo_decoder_banco_3_num_reg,
       modulo_decoder_banco_4_code, modulo_decoder_banco_4_num_reg, modulo_decoder_registro_1_codea,
       modulo_decoder_registro_1_codeb;
  wire [7:0] banco_4registros_1_out_6, banco_4registros_2_out_6, banco_4registros_3_out_6,
       banco_4registros_4_out_6, modulo_decoder_banco_1_reg_input, modulo_decoder_banco_2_reg_input,
       modulo_decoder_banco_3_reg_input, modulo_decoder_banco_4_reg_input,
       modulo_decoder_registro_1_reg_inputa, modulo_decoder_registro_1_reg_inputb,
       registro_despl_universal_8bits_2_q_8bits;
  wire [15:0] demultiplexer_1_out0, demultiplexer_1_out1, demultiplexer_1_out2, demultiplexer_1_out3;

  Clock clock_1 (.out(CLK));
  Demultiplexer #(.select(2), .width(16)) demultiplexer_1 (
    .out0(demultiplexer_1_out0), .out1(demultiplexer_1_out1), .out2(demultiplexer_1_out2),
    .out3(demultiplexer_1_out3), .in(ENTRADA), .sel(ENTRADA[3:2]));
  Modulo_Decoder_Banco modulo_decoder_banco_1 (
    .In_16bits(demultiplexer_1_out0), .Reg_Input(modulo_decoder_banco_1_reg_input),
    .Code(modulo_decoder_banco_1_code), .Num_Reg(modulo_decoder_banco_1_num_reg));
  Modulo_Decoder_Banco modulo_decoder_banco_2 (
    .In_16bits(demultiplexer_1_out1), .Reg_Input(modulo_decoder_banco_2_reg_input),
    .Code(modulo_decoder_banco_2_code), .Num_Reg(modulo_decoder_banco_2_num_reg));
  Modulo_Decoder_Banco modulo_decoder_banco_3 (
    .In_16bits(demultiplexer_1_out2), .Reg_Input(modulo_decoder_banco_3_reg_input),
    .Code(modulo_decoder_banco_3_code), .Num_Reg(modulo_decoder_banco_3_num_reg));
  Modulo_Decoder_Banco modulo_decoder_banco_4 (
    .In_16bits(demultiplexer_1_out3), .Reg_Input(modulo_decoder_banco_4_reg_input),
    .Code(modulo_decoder_banco_4_code), .Num_Reg(modulo_decoder_banco_4_num_reg));
  Banco_4registros banco_4registros_1 (
    .CLK(CLK), .Reg_input(modulo_decoder_banco_1_reg_input), .Code(modulo_decoder_banco_1_code),
    .NumRegistro(modulo_decoder_banco_1_num_reg), .out_6(banco_4registros_1_out_6));  // open: Reset_Banco
  Banco_4registros banco_4registros_2 (
    .CLK(CLK), .Reg_input(modulo_decoder_banco_2_reg_input), .Code(modulo_decoder_banco_2_code),
    .NumRegistro(modulo_decoder_banco_2_num_reg), .out_6(banco_4registros_2_out_6));  // open: Reset_Banco
  Banco_4registros banco_4registros_3 (
    .CLK(CLK), .Reg_input(modulo_decoder_banco_3_reg_input), .Code(modulo_decoder_banco_3_code),
    .NumRegistro(modulo_decoder_banco_3_num_reg), .out_6(banco_4registros_3_out_6));  // open: Reset_Banco
  Banco_4registros banco_4registros_4 (
    .CLK(CLK), .Reg_input(modulo_decoder_banco_4_reg_input), .Code(modulo_decoder_banco_4_code),
    .NumRegistro(modulo_decoder_banco_4_num_reg), .out_6(banco_4registros_4_out_6));  // open: Reset_Banco
  Multiplexer #(.select(2), .width(8)) multiplexer_1 (
    .in0(banco_4registros_1_out_6), .in1(banco_4registros_2_out_6), .in2(banco_4registros_3_out_6),
    .in3(banco_4registros_4_out_6), .out(out_18), .sel(ENTRADA[3:2]));
  Modulo_Decoder_Registro modulo_decoder_registro_1 (
    .In_16bits(ENTRADA), .In_Memoria(out_18), .Reg_InputA(modulo_decoder_registro_1_reg_inputa),
    .CodeA(modulo_decoder_registro_1_codea), .Reg_InputB(modulo_decoder_registro_1_reg_inputb),
    .CodeB(modulo_decoder_registro_1_codeb));
  Registro_despl_universal_8bits registro_despl_universal_8bits_1 (
    .D_8bits(modulo_decoder_registro_1_reg_inputa), .Code(modulo_decoder_registro_1_codea), .CLK(CLK),
    .CLEAR(Clear_Cache), .Q_8bits(out_15));
  Registro_despl_universal_8bits registro_despl_universal_8bits_2 (
    .D_8bits(modulo_decoder_registro_1_reg_inputb), .Code(modulo_decoder_registro_1_codeb), .CLK(CLK),
    .CLEAR(Clear_Cache), .Q_8bits(registro_despl_universal_8bits_2_q_8bits));
  ALU_8bits alu_8bits_1 (.A(in_6), .B(in_7), .Code(in_8), .S(out_11));  // open: Cin, Cout
  ALU_8bits alu_8bits_2 (
    .A(out_15), .B(registro_despl_universal_8bits_2_q_8bits), .S(out_16), .Cout(out_17));  // open: Code, Cin

  // Notes on the sheet:
  //   8bits numero | 2bits codigo de acción | 2bits número de registro | 2bits banco/caché a modificar | 2bit  operacion (ALU)
  //   01->Carga en registro 
  //   11->Opera con ALU
  //   00-> Carga en memoria un numero
  //   10->Carga resultado de ALU en memoria
endmodule

module ALU_1bit (
  input  Cin,
  input  [1:0] Code,
  input  A,
  input  B,
  output S,
  output Cout
);

  wire adder_1_cout, adder_1_out, and_1_out, or_1_out, subtractor_1_bout, subtractor_1_out;

  and and_1 (and_1_out, A, B);
  or or_1 (or_1_out, A, B);
  Adder #(.width(1)) adder_1 (.a(A), .b(B), .out(adder_1_out), .cin(Cin), .cout(adder_1_cout));
  Subtractor #(.width(1)) subtractor_1 (.a(A), .b(B), .out(subtractor_1_out), .bin(Cin), .bout(subtractor_1_bout));
  Multiplexer #(.select(2)) multiplexer_1 (
    .in0(and_1_out), .in1(or_1_out), .in2(adder_1_out), .in3(subtractor_1_out), .out(S), .sel(Code));
  Multiplexer #(.select(2)) multiplexer_2 (
    .in0(1'b0), .in1(1'b0), .in2(adder_1_cout), .in3(subtractor_1_bout), .out(Cout), .sel(Code));
endmodule

module ALU_8bits (
  input  [7:0] A,
  input  [7:0] B,
  input  [1:0] Code,
  input  Cin,
  output [7:0] S,
  output Cout
);

  wire alu_1bit_1_cout, alu_1bit_2_cout, alu_1bit_3_cout, alu_1bit_4_cout, alu_1bit_5_cout, alu_1bit_6_cout,
       alu_1bit_7_cout;

  ALU_1bit alu_1bit_1 (.Cin(Cin), .Code(Code), .A(A[0]), .B(B[0]), .S(S[0]), .Cout(alu_1bit_1_cout));
  ALU_1bit alu_1bit_2 (.Cin(alu_1bit_1_cout), .Code(Code), .A(A[1]), .B(B[1]), .S(S[1]), .Cout(alu_1bit_2_cout));
  ALU_1bit alu_1bit_3 (.Cin(alu_1bit_2_cout), .Code(Code), .A(A[2]), .B(B[2]), .S(S[2]), .Cout(alu_1bit_3_cout));
  ALU_1bit alu_1bit_4 (.Cin(alu_1bit_3_cout), .Code(Code), .A(A[3]), .B(B[3]), .S(S[3]), .Cout(alu_1bit_4_cout));
  ALU_1bit alu_1bit_5 (.Cin(alu_1bit_4_cout), .Code(Code), .A(A[4]), .B(B[4]), .S(S[4]), .Cout(alu_1bit_5_cout));
  ALU_1bit alu_1bit_6 (.Cin(alu_1bit_5_cout), .Code(Code), .A(A[5]), .B(B[5]), .S(S[5]), .Cout(alu_1bit_6_cout));
  ALU_1bit alu_1bit_7 (.Cin(alu_1bit_6_cout), .Code(Code), .A(A[6]), .B(B[6]), .S(S[6]), .Cout(alu_1bit_7_cout));
  ALU_1bit alu_1bit_8 (.Cin(alu_1bit_7_cout), .Code(Code), .A(A[7]), .B(B[7]), .S(S[7]), .Cout(Cout));
endmodule

module Registro_8bits (
  input  [7:0] in_1,
  input  in_2,
  input  [7:0] D_in,
  input  CLK,
  input  CLEAR,
  output [7:0] out_6,
  output [7:0] Q_out
);

  Register register_1 (.D(in_1), .en(1'b1), .clk(in_2), .Q(out_6));  // open: clr
  D_Flip_Flop d_ff_1 (.D(D_in[7]), .clk(CLK), .Q(Q_out[7]), .reset(CLEAR));  // open: Qn, preset
  D_Flip_Flop d_ff_2 (.D(D_in[6]), .clk(CLK), .Q(Q_out[6]), .reset(CLEAR));  // open: Qn, preset
  D_Flip_Flop d_ff_3 (.D(D_in[5]), .clk(CLK), .Q(Q_out[5]), .reset(CLEAR));  // open: Qn, preset
  D_Flip_Flop d_ff_4 (.D(D_in[4]), .clk(CLK), .Q(Q_out[4]), .reset(CLEAR));  // open: Qn, preset
  D_Flip_Flop d_ff_5 (.D(D_in[3]), .clk(CLK), .Q(Q_out[3]), .reset(CLEAR));  // open: Qn, preset
  D_Flip_Flop d_ff_6 (.D(D_in[2]), .clk(CLK), .Q(Q_out[2]), .reset(CLEAR));  // open: Qn, preset
  D_Flip_Flop d_ff_7 (.D(D_in[1]), .clk(CLK), .Q(Q_out[1]), .reset(CLEAR));  // open: Qn, preset
  D_Flip_Flop d_ff_8 (.D(D_in[0]), .clk(CLK), .Q(Q_out[0]), .reset(CLEAR));  // open: Qn, preset
endmodule

module Registro_despl_universal_8bits (
  input  [7:0] D_8bits,
  input  [1:0] Code,
  input  CLK,
  input  CLEAR,
  output [7:0] Q_8bits
);

  wire multiplexer_1_out, multiplexer_2_out, multiplexer_3_out, multiplexer_4_out, multiplexer_5_out,
       multiplexer_6_out, multiplexer_7_out, multiplexer_8_out;

  Multiplexer #(.select(2)) multiplexer_1 (
    .in0(Q_8bits[7]), .in1(1'b0), .in2(Q_8bits[6]), .in3(D_8bits[7]), .out(multiplexer_1_out), .sel(Code));
  D_Flip_Flop d_ff_1 (.D(multiplexer_1_out), .clk(CLK), .Q(Q_8bits[7]), .reset(CLEAR));  // open: Qn, preset
  Multiplexer #(.select(2)) multiplexer_2 (
    .in0(Q_8bits[6]), .in1(Q_8bits[7]), .in2(Q_8bits[5]), .in3(D_8bits[6]), .out(multiplexer_2_out),
    .sel(Code));
  D_Flip_Flop d_ff_2 (.D(multiplexer_2_out), .clk(CLK), .Q(Q_8bits[6]), .reset(CLEAR));  // open: Qn, preset
  Multiplexer #(.select(2)) multiplexer_3 (
    .in0(Q_8bits[5]), .in1(Q_8bits[6]), .in2(Q_8bits[4]), .in3(D_8bits[5]), .out(multiplexer_3_out),
    .sel(Code));
  D_Flip_Flop d_ff_3 (.D(multiplexer_3_out), .clk(CLK), .Q(Q_8bits[5]), .reset(CLEAR));  // open: Qn, preset
  Multiplexer #(.select(2)) multiplexer_4 (
    .in0(Q_8bits[4]), .in1(Q_8bits[5]), .in2(Q_8bits[3]), .in3(D_8bits[4]), .out(multiplexer_4_out),
    .sel(Code));
  D_Flip_Flop d_ff_4 (.D(multiplexer_4_out), .clk(CLK), .Q(Q_8bits[4]), .reset(CLEAR));  // open: Qn, preset
  Multiplexer #(.select(2)) multiplexer_5 (
    .in0(Q_8bits[3]), .in1(Q_8bits[4]), .in2(Q_8bits[2]), .in3(D_8bits[3]), .out(multiplexer_5_out),
    .sel(Code));
  D_Flip_Flop d_ff_5 (.D(multiplexer_5_out), .clk(CLK), .Q(Q_8bits[3]), .reset(CLEAR));  // open: Qn, preset
  Multiplexer #(.select(2)) multiplexer_6 (
    .in0(Q_8bits[2]), .in1(Q_8bits[3]), .in2(Q_8bits[1]), .in3(D_8bits[2]), .out(multiplexer_6_out),
    .sel(Code));
  D_Flip_Flop d_ff_6 (.D(multiplexer_6_out), .clk(CLK), .Q(Q_8bits[2]), .reset(CLEAR));  // open: Qn, preset
  Multiplexer #(.select(2)) multiplexer_7 (
    .in0(Q_8bits[1]), .in1(Q_8bits[2]), .in2(Q_8bits[0]), .in3(D_8bits[1]), .out(multiplexer_7_out),
    .sel(Code));
  D_Flip_Flop d_ff_7 (.D(multiplexer_7_out), .clk(CLK), .Q(Q_8bits[1]), .reset(CLEAR));  // open: Qn, preset
  Multiplexer #(.select(2)) multiplexer_8 (
    .in0(Q_8bits[0]), .in1(Q_8bits[1]), .in2(1'b0), .in3(D_8bits[0]), .out(multiplexer_8_out), .sel(Code));
  D_Flip_Flop d_ff_8 (.D(multiplexer_8_out), .clk(CLK), .Q(Q_8bits[0]), .reset(CLEAR));  // open: Qn, preset

  // Notes on the sheet:
  //   00 keep 01 shift right 10 shift left 11 load
endmodule

module Banco_4registros (
  input  CLK,
  input  Reset_Banco,
  input  [7:0] Reg_input,
  input  [1:0] Code,
  input  [1:0] NumRegistro,
  output [7:0] out_6
);

  wire [7:0] registro_despl_universal_8bits_1_q_8bits, registro_despl_universal_8bits_2_q_8bits,
       registro_despl_universal_8bits_3_q_8bits, registro_despl_universal_8bits_4_q_8bits;
  wire [9:0] demultiplexer_1_out0, demultiplexer_1_out1, demultiplexer_1_out2, demultiplexer_1_out3;

  Demultiplexer #(.select(2), .width(10)) demultiplexer_1 (
    .out0(demultiplexer_1_out0), .out1(demultiplexer_1_out1), .out2(demultiplexer_1_out2),
    .out3(demultiplexer_1_out3), .in({Code, Reg_input}), .sel(NumRegistro));
  Registro_despl_universal_8bits registro_despl_universal_8bits_1 (
    .D_8bits(demultiplexer_1_out0[7:0]), .Code(demultiplexer_1_out0[9:8]), .CLK(CLK), .CLEAR(Reset_Banco),
    .Q_8bits(registro_despl_universal_8bits_1_q_8bits));
  Registro_despl_universal_8bits registro_despl_universal_8bits_2 (
    .D_8bits(demultiplexer_1_out1[7:0]), .Code(demultiplexer_1_out1[9:8]), .CLK(CLK), .CLEAR(Reset_Banco),
    .Q_8bits(registro_despl_universal_8bits_2_q_8bits));
  Registro_despl_universal_8bits registro_despl_universal_8bits_3 (
    .D_8bits(demultiplexer_1_out2[7:0]), .Code(demultiplexer_1_out2[9:8]), .CLK(CLK), .CLEAR(Reset_Banco),
    .Q_8bits(registro_despl_universal_8bits_3_q_8bits));
  Registro_despl_universal_8bits registro_despl_universal_8bits_4 (
    .D_8bits(demultiplexer_1_out3[7:0]), .Code(demultiplexer_1_out3[9:8]), .CLK(CLK), .CLEAR(Reset_Banco),
    .Q_8bits(registro_despl_universal_8bits_4_q_8bits));
  Multiplexer #(.select(2), .width(8)) multiplexer_1 (
    .in0(registro_despl_universal_8bits_1_q_8bits), .in1(registro_despl_universal_8bits_2_q_8bits),
    .in2(registro_despl_universal_8bits_3_q_8bits), .in3(registro_despl_universal_8bits_4_q_8bits),
    .out(out_6), .sel(NumRegistro));
endmodule

module Modulo_Decoder_Banco (
  input  [15:0] In_16bits,
  output [7:0] Reg_Input,
  output [1:0] Code,
  output [1:0] Num_Reg
);

  Multiplexer #(.select(2), .width(12)) multiplexer_1 (
    .in0(In_16bits[15:4]), .in1({{10{1'b0}}, In_16bits[5:4]}), .in2({12{1'b0}}), .in3({12{1'b0}}),
    .out({Reg_Input, Code, Num_Reg}), .sel(In_16bits[1:0]));

  // Notes on the sheet:
  //   Numero
  //   8bits numero | 2bits codigo de acción | 2bits número de registro | 2bits banco/caché a modificar | 1bit  operacion (ALU)
endmodule

module Modulo_Decoder_Registro (
  input  [15:0] In_16bits,
  input  [7:0] In_Memoria,
  output [7:0] Reg_InputA,
  output [1:0] CodeA,
  output [7:0] Reg_InputB,
  output [1:0] CodeB
);

  wire multiplexer_3_out;
  wire [1:0] multiplexer_4_out;
  wire [7:0] multiplexer_2_out;
  wire [15:0] demultiplexer_1_out0, multiplexer_1_out;

  Multiplexer #(.select(2), .width(16)) multiplexer_1 (
    .in0({16{1'b0}}), .in1(In_16bits), .in2({16{1'b0}}), .in3({16{1'b0}}), .out(multiplexer_1_out),
    .sel(In_16bits[1:0]));
  Demultiplexer #(.width(16)) demultiplexer_1 (
    .out0(demultiplexer_1_out0), .in(multiplexer_1_out), .sel(In_16bits[7]));  // open: out1
  Multiplexer #(.width(8)) multiplexer_2 (
    .in0(demultiplexer_1_out0[15:8]), .in1(In_Memoria), .out(multiplexer_2_out), .sel(In_16bits[7]));
  Multiplexer multiplexer_3 (
    .in0(demultiplexer_1_out0[2]), .in1(In_16bits[6]), .out(multiplexer_3_out), .sel(In_16bits[7]));
  Multiplexer #(.width(2)) multiplexer_4 (
    .in0(demultiplexer_1_out0[4:3]), .in1({2{In_16bits[7]}}), .out(multiplexer_4_out), .sel(In_16bits[7]));
  Demultiplexer #(.width(8)) demultiplexer_2 (
    .out0(Reg_InputA), .out1(Reg_InputB), .in(multiplexer_2_out), .sel(multiplexer_3_out));
  Demultiplexer #(.width(2)) demultiplexer_3 (
    .out0(CodeA), .out1(CodeB), .in(multiplexer_4_out), .sel(multiplexer_3_out));

  // Other names for the same wires on the sheet: Option01 = In_16bits[7]

  // Notes on the sheet:
  //   Numero
endmodule
